# Fritzing sketch schematic (saved by Fritzing 0.9.3b)

parts:
  M2 = DC Motor
  M4 = DC Motor
  M5 = DC Motor
  Part2 = Adafruit Motor/Stepper/Servo Shield [part_number="Adafruit #1438"]
  M6 = DC Motor

nets:
  N1: M2.pin_1, Part2.M2A
  N2: M2.pin_2, Part2.M2B
  N3: M4.pin_1, Part2.M3B
  N4: M4.pin_2, Part2.M3A
  N5: M5.pin_1, Part2.M1B
  N6: M5.pin_2, Part2.M1A
  N7: Part2.M4B, M6.pin_2
  N8: Part2.M4A, M6.pin_1

notes:
  FRONT

custom parts:
  Adafruit Motor/Stepper/Servo Shield: The original Adafruit Motorshield kit is one of our most beloved kits, which is why we decided to make something even better. We have upgraded the shield kit to make the bestest, easiest way to drive DC and Stepper motors. This shield will make quick work of your next robotics project! We kept the ability to drive up to 4 DC motors or 2 stepper motors, but added many improvements: Instead of a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
